// Logisim project NAND.circ as structural Verilog: 7 circuits, main circuit main
module main (
  input  A,
  input  B,
  input  Selection,
  output out_4
);

  Multiplexer multiplexer_1 (.in0(A), .in1(B), .out(out_4), .sel(Selection));
endmodule

module NAND_Gate (
  input  A,
  input  B
);

  wire nand_1_out;

  nand nand_1 (nand_1_out, A, B);
  LED led_1 (.in(nand_1_out));
endmodule

module NOT_Gate (
  input  A,
  output Q
);

  nand nand_1 (Q, A, A);
endmodule

module AND_Gate (
  input  A,
  input  B,
  input  C,
  output Q
);

  and and_1 (Q, A, B, C);
endmodule

module OR_Gate (
  input  A,
  input  B,
  output Q
);

  or or_1 (Q, A, B);
endmodule

module XOR_Gate (
  input  A,
  input  B,
  output Q
);

  xor xor_1 (Q, A, B);
endmodule

module MUX (
  input  A,
  input  Selection,
  input  B,
  output Q
);

  wire n1_out, n2_out, not_1_out;

  nand n1 (n1_out, A, not_1_out);
  not not_1 (not_1_out, Selection);
  nand n2 (n2_out, Selection, B);
  nand n3 (Q, n1_out, n2_out);
endmodule
